# Fritzing sketch LightGary (saved by Fritzing 0.9.2b)
circuit board: 15.1465cm x 7.82121cm
breadboards: 2

parts:
  Bauteil1 = Arduino Uno (Rev3)
  LED1 = RGB LED - (4 legs) [package="5 mm [THT]"]
  ENCODER1 = Rotary Encoder with Knob
  U1 = 74HC595 [package="DIP16 [THT]"]
  RTC1 = DS1307 RTC Breakout
  U2 = 74HC595 [package="DIP16 [THT]"]
  U3 = 74HC595 [package="DIP16 [THT]"]
  R2 = Resistor [tolerance=±2% resistance=270 package=THT]
  R3 = Resistor [tolerance=±2% resistance=270 package=THT]
  R5 = Resistor [tolerance=±2% resistance=270 package=THT]
  R6 = Resistor [tolerance=±2% resistance=270 package=THT]
  R7 = Resistor [tolerance=±2% resistance=270 package=THT]
  R8 = Resistor [tolerance=±2% resistance=270 package=THT]
  R9 = Resistor [tolerance=±2% resistance=270 package=THT]
  R10 = Resistor [tolerance=±2% resistance=270 package=THT]
  R11 = Resistor [tolerance=±2% resistance=270 package=THT]
  C1 = Electrolytic Capacitor [capacitance=1mF package="100 mil [THT, electrolytic]"]
  J1 = female pin header, 8 pins [form="♀ (female)"]
  J3 = female pin header, 8 pins [form="♀ (female)"]
  R15 = Resistor [tolerance=±2% resistance=270 package=THT]
  R16 = Resistor [tolerance=±2% resistance=270 package=THT]
  R17 = Resistor [tolerance=±2% resistance=330 package=THT]
  R18 = Resistor [tolerance=±2% resistance=330 package=THT]
  R19 = Resistor [tolerance=±2% resistance=330 package=THT]
  R21 = Resistor [tolerance=±5% resistance=10k package=THT]
  R22 = Resistor [tolerance=±5% resistance=10k package=THT]
  R23 = Resistor [tolerance=±5% resistance=10k package=THT]
  J4 = female pin header, 3 pins [form="♀ (female)"]  # not connected
  J5 = female pin header, 5 pins [form="♀ (female)"]  # not connected
  neopixel1 = Neopixel 24 Ring  # not connected

nets:
  N1: Bauteil1.A1, U2.SH_CP, U3.SH_CP
  N2: Bauteil1.A2, U2.ST_CP, U3.ST_CP
  N3: Bauteil1.A3, U2.DS
  N4: Bauteil1.D8, ENCODER1.no_name_yet#4, R23.Pin_1
  N5: Bauteil1.D11_PWM/MOSI, U1.DS
  N6: Bauteil1.D13/SCK, U1.SH_CP
  GND: Bauteil1.GND, ENCODER1.no_name_yet#2, ENCODER1.no_name_yet#5, U1.GND, U1.OE, RTC1.GND, U2.GND, U2.OE, U3.GND, U3.OE, C1.-
  N7: Bauteil1.D2, ENCODER1.no_name_yet#1, R21.Pin_1
  N8: Bauteil1.D4, ENCODER1.no_name_yet#3, R22.Pin_0
  N9: Bauteil1.D7, U1.ST_CP
  VCC: Bauteil1.5V, LED1.common_anode, U1.MR, U1.VCC, RTC1.5V, U2.MR, U2.VCC, U3.MR, U3.VCC, C1.+, R21.Pin_0, R22.Pin_1, R23.Pin_0
  N10: LED1.red_cathode, R17.Pin_1
  N11: LED1.green_cathode, R18.Pin_1
  N12: LED1.blue_cathode, R19.Pin_1
  N13: U1.Q1, R18.Pin_0
  N14: U1.Q2, R19.Pin_0
  N15: U1.Q0, R17.Pin_0
  N16: U2.Q1, J3.pin2
  N17: U2.Q2, J3.pin3
  N18: U2.Q3, J3.pin4
  N19: U2.Q4, J3.pin5
  N20: U2.Q5, R16.Pin_0
  N21: U2.Q6, R15.Pin_0
  N22: U2.Q7, R3.Pin_0
  N23: U2.Q7', U3.DS
  N24: U2.Q0, J3.pin1
  N25: U3.Q1, R2.Pin_0
  N26: U3.Q2, R9.Pin_0
  N27: U3.Q3, R8.Pin_0
  N28: U3.Q4, R7.Pin_0
  N29: U3.Q5, R6.Pin_0
  N30: U3.Q6, R5.Pin_0
  N31: U3.Q7, R11.Pin_1
  N32: U3.Q0, R10.Pin_1
  N33: R2.Pin_1, J1.pin2
  N34: R3.Pin_1, J3.pin8
  N35: R5.Pin_1, J1.pin7
  N36: R6.Pin_1, J1.pin6
  N37: R7.Pin_1, J1.pin5
  N38: R8.Pin_1, J1.pin4
  N39: R9.Pin_1, J1.pin3
  N40: R10.Pin_0, J1.pin1
  N41: R11.Pin_0, J1.pin8
  N42: J3.pin6, R16.Pin_1
  N43: J3.pin7, R15.Pin_1

custom parts:
  Rotary Encoder with Knob: Rotary Encoder with 1/4" Shaft and Knob
  DS1307 RTC Breakout: DS1307 Real-time Clock Breakout Board with Battery
